# Fritzing sketch Schematic (saved by Fritzing 0.9.8b)

parts:
  Mod1 = Raspberry Pi 4B
  VCC1 = Battery
  Hat4 = 4WD Hat [package="DIP (Dual Inline) [THT]"]
  M1 = Dagu DGServo 9g (Top view) [part_number=RS001B]
  M2 = gear-motor
  M3 = gear-motor
  M4 = gear-motor
  M5 = gear-motor
  HC-SR04_Sensor_1 = HC-SR04 Ultrasonic Distance Sensor
  Part1 = FC-03 [chip_label=FC-03]
  U1 = TCM8240MD [package=tcm8240md]  # not connected

nets:
  N1: Mod1.3V3, Hat4.GPIO2, Hat4.GPIO_17
  N2: Mod1.5V, Hat4.GPIO1, Hat4.GPIO3
  N3: Mod1.GPIO2, Hat4.GPIO4
  N4: Mod1.GPIO3, Hat4.GPIO5
  N5: Mod1.GND, Hat4.GPIO6, Hat4.GPIO_9, Hat4.GPIO_14, Hat4.GPIO_20, Hat4.GPIO_26, Hat4.GPIO_29, Hat4.GPIO_33, Hat4.GPIO_39
  N6: Mod1.GPIO4, Hat4.GPIO7
  N7: Mod1.GPIO14, Hat4.GPIO8
  N8: Mod1.GPIO15, Hat4.GPIO_10
  N9: Mod1.GPIO17, Hat4.GPIO_11
  N10: Mod1.GPIO18, Hat4.GPIO_12
  N11: Mod1.GPIO27, Hat4.GPIO_13
  N12: Mod1.GPIO22, Hat4.GPIO_15
  N13: Mod1.GPIO23, Hat4.GPIO_16
  N14: Mod1.GPIO24, Hat4.GPIO_18
  N15: Mod1.GPIO10, Hat4.GPIO_19
  N16: Mod1.GPIO9, Hat4.GPIO_21
  N17: Mod1.GPIO25, Hat4.GPIO_22
  N18: Mod1.GPIO11, Hat4.GPIO_23
  N19: Mod1.GPIO8, Hat4.GPIO_24
  N20: Mod1.GPIO7, Hat4.GPIO_25
  N21: Mod1.ID_SD, Hat4.GPIO_27
  N22: Mod1.ID_SC, Hat4.GPIO_28
  N23: Mod1.GPIO5, Hat4.GPIO_30
  N24: Mod1.GPIO6, Hat4.GPIO_32
  N25: Mod1.GPIO12, Hat4.GPIO_31
  N26: Mod1.GPIO13, Hat4.GPIO_34
  N27: Mod1.GPIO19, Hat4.GPIO_35
  N28: Mod1.GPIO16, Hat4.GPIO_36
  N29: Mod1.GPIO26, Hat4.GPIO_37
  N30: Mod1.GPIO20, Hat4.GPIO_38
  N31: Mod1.GPIO21, Hat4.GPIO40
  N32: VCC1.-, Hat4.power_2
  N33: VCC1.+, Hat4.power_1
  N34: Hat4.motor_1a, M3.pin_2
  N35: Hat4.moto_1b, M3.pin_1
  N36: Hat4.motor_2a, M2.pin_2
  N37: Hat4.motor_2b, M2.pin_1
  N38: Hat4.servo_1, M1.gnd
  N39: Hat4.servo_2, M1.vcc
  N40: Hat4.servo_3, M1.pulse
  N41: Hat4.motor_3a, M4.pin_2
  N42: Hat4.motor_3b, M4.pin_1
  N43: Hat4.motor_4a, M5.pin_2
  N44: Hat4.motor_4b, M5.pin_1
  N45: Hat4.ultrasonic_1, HC-SR04_Sensor_1.VCC
  N46: Hat4.ultrasonic_2, HC-SR04_Sensor_1.TRIG
  N47: Hat4.ultrasonic_3, HC-SR04_Sensor_1.ECHO
  N48: Hat4.ultrasonic_4, HC-SR04_Sensor_1.GND
  N49: Hat4.phoro-interrupter_1, Part1.GND
  N50: Hat4.phoro-interrupter_2, Part1.3v3
  N51: Hat4.phoro-interrupter_3, Part1.S0
  N52: Hat4.phoro-interrupter_4, Part1.S1

custom parts:
  4WD Hat: PICAR Hat
  FC-03: FC-03, LM393 IR Speed Sensor Encoder
